// Logisim project RISCV.circ as structural Verilog
module main (
  input  in_1
);

  wire clk, d_rd, d_we;
  wire [31:0] d_adr, d_din, d_dout, i_adr, i_din;

  ROM #(.addrWidth(13), .dataWidth(32), .misaligned("true")) rom_1 (.addr(i_adr[14:2]), .data(i_din));
  Clock clock_1 (.out(clk));
  core core_1 (
    .d_din(d_din), .d_rdy(1'b1), .i_din(i_din), .i_rdy(1'b1), .clk(clk), .rst(in_1), .d_dout(d_dout),
    .d_adr(d_adr), .d_we(d_we), .d_rd(d_rd), .i_adr(i_adr));  // open: enB, i_rd
  // Probe on d_adr[7:0]
  RAM #(.asyncread("true"), .dataWidth(32)) ram_1 (
    .addr(d_adr[7:0]), .we(d_we), .oe(d_rd), .clk(clk), .din(d_dout), .dout(d_din));
  // Probe on d_dout

  // Other names for the same wires on the sheet: rst = in_1

  // Notes on the sheet:
  //   contents of rom_1 (hex, n*v repeats v):
  //   ff00113 8000ef 6f ff010113 112623 15600793 f02823 1002503 1002583 18000ef c12083 a02a23 513 1010113
  //   8067 50613 513 15f693 68463 c50533 15d593 161613 fe0596e3 8067
endmodule

module barrelShifterLeft (
  input  [31:0] s1,
  input  arith,
  input  [4:0] s2,
  output [31:0] d
);

  wire arith_t;
  wire [31:0] multiplexer_1_out, multiplexer_2_out, multiplexer_3_out, multiplexer_4_out;

  and and_1 (arith_t, s1[31], arith);
  Multiplexer #(.width(32)) multiplexer_1 (.in0(s1), .in1({arith_t, s1[31:1]}), .out(multiplexer_1_out), .sel(s2[0]));
  Multiplexer #(.width(32)) multiplexer_2 (
    .in0(multiplexer_1_out), .in1({{2{arith_t}}, multiplexer_1_out[31:2]}), .out(multiplexer_2_out),
    .sel(s2[1]));
  Multiplexer #(.width(32)) multiplexer_3 (
    .in0(multiplexer_2_out), .in1({{4{arith_t}}, multiplexer_2_out[31:4]}), .out(multiplexer_3_out),
    .sel(s2[2]));
  Multiplexer #(.width(32)) multiplexer_4 (
    .in0(multiplexer_3_out), .in1({{8{arith_t}}, multiplexer_3_out[31:8]}), .out(multiplexer_4_out),
    .sel(s2[3]));
  Multiplexer #(.width(32)) multiplexer_5 (
    .in0(multiplexer_4_out), .in1({{16{arith_t}}, multiplexer_4_out[31:16]}), .out(d), .sel(s2[4]));
endmodule

// SRA&L
module barrelShifterRight (
  input  [31:0] s1,
  input  arith,
  input  [4:0] s2,
  output [31:0] d
);

  wire arith_t;
  wire [31:0] multiplexer_1_out, multiplexer_2_out, multiplexer_3_out, multiplexer_4_out;

  and and_1 (arith_t, s1[31], arith);
  Multiplexer #(.width(32)) multiplexer_1 (.in0(s1), .in1({arith_t, s1[31:1]}), .out(multiplexer_1_out), .sel(s2[0]));
  Multiplexer #(.width(32)) multiplexer_2 (
    .in0(multiplexer_1_out), .in1({{2{arith_t}}, multiplexer_1_out[31:2]}), .out(multiplexer_2_out),
    .sel(s2[1]));
  Multiplexer #(.width(32)) multiplexer_3 (
    .in0(multiplexer_2_out), .in1({{4{arith_t}}, multiplexer_2_out[31:4]}), .out(multiplexer_3_out),
    .sel(s2[2]));
  Multiplexer #(.width(32)) multiplexer_4 (
    .in0(multiplexer_3_out), .in1({{8{arith_t}}, multiplexer_3_out[31:8]}), .out(multiplexer_4_out),
    .sel(s2[3]));
  Multiplexer #(.width(32)) multiplexer_5 (
    .in0(multiplexer_4_out), .in1({{16{arith_t}}, multiplexer_4_out[31:16]}), .out(d), .sel(s2[4]));
endmodule

module alu (
  input  [31:0] s1,
  input  [31:0] s2,
  input  alt,
  input  [2:0] opcode,
  input  brchEn,
  output [31:0] d,
  output branch
);

  wire and_1_out, C, eq, ge, lt, ltu, multiplexer_3_out, ne, or_2_out, or_3_out;
  wire [31:0] adder_1_out, and_2_out, barrelshifterright_1_d, bit_extender_1_out, bit_extender_2_out,
       multiplexer_1_out, not_1_out, or_1_out, shifter_1_out, xor_1_out;

  assign not_1_out = ~s2;  // NOT_Gate not_1, 32 bits wide
  Adder #(.width(32)) adder_1 (.a(s1), .b(multiplexer_1_out), .out(adder_1_out), .cin(alt), .cout(C));
  Multiplexer #(.width(32)) multiplexer_1 (.in0(s2), .in1(not_1_out), .out(multiplexer_1_out), .sel(alt));
  and and_1 (and_1_out, s1[31], adder_1_out[31]);
  Shifter #(.width(32)) shifter_1 (.in(s1), .\dist (s2[4:0]), .out(shifter_1_out));
  assign xor_1_out = s1 ^ s2;  // XOR_Gate xor_1, 32 bits wide
  assign or_1_out = s1 | s2;  // OR_Gate or_1, 32 bits wide
  assign and_2_out = s1 & s2;  // AND_Gate and_2, 32 bits wide
  or or_2 (or_2_out, s1[31], adder_1_out[31]);
  and and_3 (lt, or_2_out, or_3_out);
  or or_3 (or_3_out, not_1_out[31], and_1_out);
  not not_2 (ltu, C);
  not not_3 (ge, lt);
  barrelShifterRight barrelshifterright_1 (.s1(s1), .arith(alt), .s2(s2[4:0]), .d(barrelshifterright_1_d));
  Comparator #(.width(32)) comparator_1 (.a({32{1'b0}}), .b(adder_1_out), .eq(eq));  // open: gt, lt
  assign bit_extender_1_out = {{31{1'b0}}, lt};  // Bit_Extender bit_extender_1
  assign bit_extender_2_out = {{31{1'b0}}, ltu};  // Bit_Extender bit_extender_2
  not not_4 (ne, eq);
  Multiplexer #(.select(3), .width(32)) multiplexer_2 (
    .in0(adder_1_out), .in1(shifter_1_out), .in2(bit_extender_1_out), .in3(bit_extender_2_out),
    .in4(xor_1_out), .in5(barrelshifterright_1_d), .in6(or_1_out), .in7(and_2_out), .out(d), .sel(opcode));
  Multiplexer #(.select(3)) multiplexer_3 (
    .in0(eq), .in1(ne), .in4(lt), .in5(ge), .in6(ltu), .in7(C), .out(multiplexer_3_out), .sel(opcode));  // open: in2, in3
  and and_4 (branch, multiplexer_3_out, brchEn);

  // Other names for the same wires on the sheet: geu = C
endmodule

module regFile (
  input  [31:0] d,
  input  wEn,
  input  [4:0] rs1,
  input  [4:0] rd,
  input  [4:0] rs2,
  input  CLK,
  output [31:0] s1,
  output [31:0] s2
);

  wire demultiplexer_1_out0, demultiplexer_1_out1, demultiplexer_1_out2, demultiplexer_1_out3,
       demultiplexer_1_out4, demultiplexer_1_out5, demultiplexer_1_out6, demultiplexer_1_out7,
       demultiplexer_1_out8, demultiplexer_1_out9, demultiplexer_1_out10, demultiplexer_1_out11,
       demultiplexer_1_out12, demultiplexer_1_out13, demultiplexer_1_out14, demultiplexer_1_out15,
       demultiplexer_1_out16, demultiplexer_1_out17, demultiplexer_1_out18, demultiplexer_1_out19,
       demultiplexer_1_out20, demultiplexer_1_out21, demultiplexer_1_out22, demultiplexer_1_out23,
       demultiplexer_1_out24, demultiplexer_1_out25, demultiplexer_1_out26, demultiplexer_1_out27,
       demultiplexer_1_out28, demultiplexer_1_out29, demultiplexer_1_out30, demultiplexer_1_out31;
  wire [31:0] register_1_q, register_2_q, register_3_q, register_4_q, register_5_q, register_6_q,
       register_7_q, register_8_q, register_9_q, register_10_q, register_11_q, register_12_q, register_13_q,
       register_14_q, register_15_q, register_16_q, register_17_q, register_18_q, register_19_q,
       register_20_q, register_21_q, register_22_q, register_23_q, register_24_q, register_25_q,
       register_26_q, register_27_q, register_28_q, register_29_q, register_30_q, register_31_q;

  Demultiplexer #(.select(5)) demultiplexer_1 (
    .out0(demultiplexer_1_out0), .out1(demultiplexer_1_out1), .out2(demultiplexer_1_out2),
    .out3(demultiplexer_1_out3), .out4(demultiplexer_1_out4), .out5(demultiplexer_1_out5),
    .out6(demultiplexer_1_out6), .out7(demultiplexer_1_out7), .out8(demultiplexer_1_out8),
    .out9(demultiplexer_1_out9), .out10(demultiplexer_1_out10), .out11(demultiplexer_1_out11),
    .out12(demultiplexer_1_out12), .out13(demultiplexer_1_out13), .out14(demultiplexer_1_out14),
    .out15(demultiplexer_1_out15), .out16(demultiplexer_1_out16), .out17(demultiplexer_1_out17),
    .out18(demultiplexer_1_out18), .out19(demultiplexer_1_out19), .out20(demultiplexer_1_out20),
    .out21(demultiplexer_1_out21), .out22(demultiplexer_1_out22), .out23(demultiplexer_1_out23),
    .out24(demultiplexer_1_out24), .out25(demultiplexer_1_out25), .out26(demultiplexer_1_out26),
    .out27(demultiplexer_1_out27), .out28(demultiplexer_1_out28), .out29(demultiplexer_1_out29),
    .out30(demultiplexer_1_out30), .out31(demultiplexer_1_out31), .in(wEn), .sel(rd));
  Register #(.width(32)) register_1 (.D(d), .en(demultiplexer_1_out1), .Q(register_1_q), .clk(CLK));  // open: clr
  Register #(.width(32)) register_2 (.D(d), .en(demultiplexer_1_out2), .Q(register_2_q), .clk(CLK));  // open: clr
  Register #(.width(32)) register_3 (.D(d), .en(demultiplexer_1_out3), .Q(register_3_q), .clk(CLK));  // open: clr
  Register #(.width(32)) register_4 (.D(d), .en(demultiplexer_1_out4), .Q(register_4_q), .clk(CLK));  // open: clr
  Register #(.width(32)) register_5 (.D(d), .en(demultiplexer_1_out5), .Q(register_5_q), .clk(CLK));  // open: clr
  Register #(.width(32)) register_6 (.D(d), .en(demultiplexer_1_out6), .Q(register_6_q), .clk(CLK));  // open: clr
  Register #(.width(32)) register_7 (.D(d), .en(demultiplexer_1_out7), .Q(register_7_q), .clk(CLK));  // open: clr
  Register #(.width(32)) register_8 (.D(d), .en(demultiplexer_1_out8), .Q(register_8_q), .clk(CLK));  // open: clr
  Register #(.width(32)) register_9 (.D(d), .en(demultiplexer_1_out9), .Q(register_9_q), .clk(CLK));  // open: clr
  Register #(.width(32)) register_10 (.D(d), .en(demultiplexer_1_out10), .Q(register_10_q), .clk(CLK));  // open: clr
  Register #(.width(32)) register_11 (.D(d), .en(demultiplexer_1_out11), .Q(register_11_q), .clk(CLK));  // open: clr
  Register #(.width(32)) register_12 (.D(d), .en(demultiplexer_1_out12), .Q(register_12_q), .clk(CLK));  // open: clr
  Register #(.width(32)) register_13 (.D(d), .en(demultiplexer_1_out13), .Q(register_13_q), .clk(CLK));  // open: clr
  Register #(.width(32)) register_14 (.D(d), .en(demultiplexer_1_out14), .Q(register_14_q), .clk(CLK));  // open: clr
  Register #(.width(32)) register_15 (.D(d), .en(demultiplexer_1_out15), .Q(register_15_q), .clk(CLK));  // open: clr
  Register #(.width(32)) register_16 (.D(d), .en(demultiplexer_1_out16), .Q(register_16_q), .clk(CLK));  // open: clr
  Register #(.width(32)) register_17 (.D(d), .en(demultiplexer_1_out17), .Q(register_17_q), .clk(CLK));  // open: clr
  Register #(.width(32)) register_18 (.D(d), .en(demultiplexer_1_out18), .Q(register_18_q), .clk(CLK));  // open: clr
  Register #(.width(32)) register_19 (.D(d), .en(demultiplexer_1_out19), .Q(register_19_q), .clk(CLK));  // open: clr
  Register #(.width(32)) register_20 (.D(d), .en(demultiplexer_1_out20), .Q(register_20_q), .clk(CLK));  // open: clr
  Register #(.width(32)) register_21 (.D(d), .en(demultiplexer_1_out21), .Q(register_21_q), .clk(CLK));  // open: clr
  Register #(.width(32)) register_22 (.D(d), .en(demultiplexer_1_out22), .Q(register_22_q), .clk(CLK));  // open: clr
  Register #(.width(32)) register_23 (.D(d), .en(demultiplexer_1_out23), .Q(register_23_q), .clk(CLK));  // open: clr
  Register #(.width(32)) register_24 (.D(d), .en(demultiplexer_1_out24), .Q(register_24_q), .clk(CLK));  // open: clr
  Register #(.width(32)) register_25 (.D(d), .en(demultiplexer_1_out25), .Q(register_25_q), .clk(CLK));  // open: clr
  Register #(.width(32)) register_26 (.D(d), .en(demultiplexer_1_out26), .Q(register_26_q), .clk(CLK));  // open: clr
  Register #(.width(32)) register_27 (.D(d), .en(demultiplexer_1_out27), .Q(register_27_q), .clk(CLK));  // open: clr
  Register #(.width(32)) register_28 (.D(d), .en(demultiplexer_1_out28), .Q(register_28_q), .clk(CLK));  // open: clr
  Register #(.width(32)) register_29 (.D(d), .en(demultiplexer_1_out29), .Q(register_29_q), .clk(CLK));  // open: clr
  Register #(.width(32)) register_30 (.D(d), .en(demultiplexer_1_out30), .Q(register_30_q), .clk(CLK));  // open: clr
  Register #(.width(32)) register_31 (.D(d), .en(demultiplexer_1_out31), .Q(register_31_q), .clk(CLK));  // open: clr
  Multiplexer #(.select(5), .width(32)) multiplexer_1 (
    .in0({32{1'b0}}), .in1(register_1_q), .in2(register_2_q), .in3(register_3_q), .in4(register_4_q),
    .in5(register_5_q), .in6(register_6_q), .in7(register_7_q), .in8(register_8_q), .in9(register_9_q),
    .in10(register_10_q), .in11(register_11_q), .in12(register_12_q), .in13(register_13_q),
    .in14(register_14_q), .in15(register_15_q), .in16(register_16_q), .in17(register_17_q),
    .in18(register_18_q), .in19(register_19_q), .in20(register_20_q), .in21(register_21_q),
    .in22(register_22_q), .in23(register_23_q), .in24(register_24_q), .in25(register_25_q),
    .in26(register_26_q), .in27(register_27_q), .in28(register_28_q), .in29(register_29_q),
    .in30(register_30_q), .in31(register_31_q), .out(s1), .sel(rs1));
  Multiplexer #(.select(5), .width(32)) multiplexer_2 (
    .in0({32{1'b0}}), .in1(register_1_q), .in2(register_2_q), .in3(register_3_q), .in4(register_4_q),
    .in5(register_5_q), .in6(register_6_q), .in7(register_7_q), .in8(register_8_q), .in9(register_9_q),
    .in10(register_10_q), .in11(register_11_q), .in12(register_12_q), .in13(register_13_q),
    .in14(register_14_q), .in15(register_15_q), .in16(register_16_q), .in17(register_17_q),
    .in18(register_18_q), .in19(register_19_q), .in20(register_20_q), .in21(register_21_q),
    .in22(register_22_q), .in23(register_23_q), .in24(register_24_q), .in25(register_25_q),
    .in26(register_26_q), .in27(register_27_q), .in28(register_28_q), .in29(register_29_q),
    .in30(register_30_q), .in31(register_31_q), .out(s2), .sel(rs2));
endmodule

module immDecoder (
  input  [31:0] inst,
  input  [2:0] instype,
  output [31:0] imm
);

  Multiplexer #(.select(3), .width(32)) multiplexer_1 (
    .in0({32{1'b0}}), .in1({{21{inst[31]}}, inst[30:20]}), .in2({{21{inst[31]}}, inst[30:25], inst[11:7]}),
    .in3({{20{inst[31]}}, inst[7], inst[30:25], inst[11:8], 1'b0}), .in4({inst[31:12], {12{1'b0}}}),
    .in5({{12{inst[31]}}, inst[19:12], inst[20], inst[30:21], 1'b0}), .in6({32{1'b0}}), .in7({32{1'b0}}),
    .out(imm), .sel(instype));
endmodule

module pc (
  input  [31:0] imm,
  input  [31:0] d,
  input  brch,
  input  pcsrc,
  input  en,
  input  clk,
  input  rst,
  output [31:0] adr4,
  output [31:0] adr
);

  wire adder_1_cout;
  wire [31:0] adder_2_out, multiplexer_1_out, multiplexer_2_out;

  Adder #(.width(32)) adder_1 (.a(adr), .b(32'h4), .out(adr4), .cout(adder_1_cout));  // open: cin
  Adder #(.width(32)) adder_2 (.a(adr), .b(imm), .out(adder_2_out), .cin(adder_1_cout));  // open: cout
  Multiplexer #(.width(32)) multiplexer_1 (.in0(adr4), .in1(adder_2_out), .out(multiplexer_1_out), .sel(brch));
  Multiplexer #(.width(32)) multiplexer_2 (.in0(multiplexer_1_out), .in1(d), .out(multiplexer_2_out), .sel(pcsrc));
  Register #(.width(32)) register_1 (.D(multiplexer_2_out), .en(en), .Q(adr), .clk(clk), .clr(rst));
endmodule

module core (
  input  [31:0] d_din,
  input  d_rdy,
  input  [31:0] i_din,
  input  i_rdy,
  input  clk,
  input  rst,
  output [31:0] d_dout,
  output [31:0] d_adr,
  output d_we,
  output d_rd,
  output [3:0] enB,
  output [31:0] i_adr,
  output i_rd
);

  wire altAlu, brch, brchEn, enPc, pcSrc, selS1Alu, selS2Alu, wEn;
  wire [1:0] selInRd;
  wire [2:0] insType, opAlu;
  wire [31:0] immdecoder_1_imm, multiplexer_1_out, multiplexer_2_out, multiplexer_3_out, pc_1_adr4, s1,
       signextender_1_dout;

  pc pc_1 (
    .imm(immdecoder_1_imm), .d(d_adr), .brch(brch), .pcsrc(pcSrc), .en(enPc), .clk(clk), .rst(rst),
    .adr4(pc_1_adr4), .adr(i_adr));
  // Probe on i_din
  Multiplexer #(.select(2), .width(32)) multiplexer_1 (
    .in0(d_adr), .in1(signextender_1_dout), .in2(immdecoder_1_imm), .in3(pc_1_adr4), .out(multiplexer_1_out),
    .sel(selInRd));
  uc uc_1 (
    .opcode(i_din[6:0]), .f7(i_din[31:25]), .f3(i_din[14:12]), .i_rdy(i_rdy), .d_rdy(d_rdy), .clk(clk),
    .rst(rst), .d_we(d_we), .d_rd(d_rd), .pcSrc(pcSrc), .i_rd(i_rd), .enPc(enPc), .selInRd(selInRd),
    .wEn(wEn), .insType(insType), .selS1Alu(selS1Alu), .selS2Alu(selS2Alu), .altAlu(altAlu), .opAlu(opAlu),
    .brchEn(brchEn));  // open: out_21
  regFile regfile_1 (
    .d(multiplexer_1_out), .wEn(wEn), .rs1(i_din[19:15]), .rd(i_din[11:7]), .rs2(i_din[24:20]), .CLK(clk),
    .s1(s1), .s2(d_dout));
  immDecoder immdecoder_1 (.inst(i_din), .instype(insType), .imm(immdecoder_1_imm));
  Multiplexer #(.width(32)) multiplexer_2 (.in0(s1), .in1(i_adr), .out(multiplexer_2_out), .sel(selS1Alu));
  Multiplexer #(.width(32)) multiplexer_3 (
    .in0(d_dout), .in1(immdecoder_1_imm), .out(multiplexer_3_out), .sel(selS2Alu));
  alu alu_1 (
    .s1(multiplexer_2_out), .s2(multiplexer_3_out), .alt(altAlu), .opcode(opAlu), .brchEn(brchEn), .d(d_adr),
    .branch(brch));
  signExtender signextender_1 (.din(d_din), .adr2(d_adr[1:0]), .exType(i_din[14:12]), .dout(signextender_1_dout));

  // Other names for the same wires on the sheet: inst[31:0] = i_din; opcode[6:0] = i_din[6:0]; rd[4:0] = i_din[11:7];
  //   f3[2:0] = i_din[14:12]; rs1[4:0] = i_din[19:15]; rs2[4:0] = i_din[24:20]; f7[6:0] = i_din[31:25];
  //   s2[31:0] = d_dout
endmodule

module uc (
  input  [6:0] opcode,
  input  [6:0] f7,
  input  [2:0] f3,
  input  i_rdy,
  input  d_rdy,
  input  clk,
  input  rst,
  output d_we,
  output d_rd,
  output pcSrc,
  output i_rd,
  output enPc,
  output [1:0] selInRd,
  output wEn,
  output [2:0] insType,
  output selS1Alu,
  output selS2Alu,
  output altAlu,
  output [2:0] opAlu,
  output brchEn,
  output out_21
);

  wire and_12_out, and_13_out, and_14_out, and_15_out, and_16_out, and_17_out, and_18_out, and_19_out, auipc,
       fence, jal, jalr, lui, not_1_out, not_2_out, not_3_out, not_4_out, not_5_out, not_6_out, not_7_out,
       not_8_out, not_9_out, not_10_out, not_11_out, not_12_out, not_13_out, not_14_out, not_15_out,
       not_16_out, not_17_out, not_18_out, not_19_out, not_20_out, not_21_out, not_22_out, not_23_out,
       not_24_out, not_25_out, not_26_out, not_27_out, not_28_out, not_29_out, not_30_out, not_31_out,
       not_32_out, not_33_out, not_34_out, not_35_out, not_36_out, not_37_out, not_38_out, op, opi, or_1_out,
       or_2_out, or_3_out, or_4_out, or_8_out, or_9_out, or_11_out, or_13_out, or_14_out, sys;
  wire [1:0] multiplexer_5_out, multiplexer_6_out, multiplexer_7_out;
  wire [2:0] multiplexer_1_out, multiplexer_2_out, multiplexer_3_out, multiplexer_4_out;

  not not_1 (not_1_out, opcode[2]);
  not not_2 (not_2_out, opcode[3]);
  not not_3 (not_3_out, opcode[4]);
  not not_4 (not_4_out, opcode[6]);
  not not_5 (not_5_out, opcode[2]);
  not not_6 (not_6_out, opcode[3]);
  not not_7 (not_7_out, opcode[4]);
  not not_8 (not_8_out, opcode[5]);
  not not_9 (not_9_out, opcode[6]);
  not not_10 (not_10_out, opcode[2]);
  not not_11 (not_11_out, opcode[3]);
  not not_12 (not_12_out, opcode[5]);
  not not_13 (not_13_out, opcode[6]);
  not not_14 (not_14_out, opcode[2]);
  not not_15 (not_15_out, opcode[3]);
  not not_16 (not_16_out, opcode[6]);
  not not_17 (not_17_out, opcode[4]);
  not not_18 (not_18_out, opcode[2]);
  not not_19 (not_19_out, opcode[3]);
  not not_20 (not_20_out, opcode[4]);
  not not_21 (not_21_out, opcode[3]);
  not not_22 (not_22_out, opcode[6]);
  not not_23 (not_23_out, opcode[2]);
  not not_24 (not_24_out, opcode[3]);
  not not_25 (not_25_out, opcode[4]);
  not not_26 (not_26_out, opcode[5]);
  not not_27 (not_27_out, opcode[6]);
  not not_28 (not_28_out, opcode[3]);
  not not_29 (not_29_out, opcode[4]);
  not not_30 (not_30_out, opcode[3]);
  not not_31 (not_31_out, opcode[5]);
  not not_32 (not_32_out, opcode[6]);
  and and_1 (d_we, opcode[0], opcode[1], not_1_out, not_2_out, not_3_out, opcode[5], not_4_out);
  and and_2 (d_rd, opcode[0], opcode[1], not_5_out, not_6_out, not_7_out, not_8_out, not_9_out);
  and and_3 (opi, opcode[0], opcode[1], not_10_out, not_11_out, opcode[4], not_12_out, not_13_out);
  and and_4 (op, opcode[0], opcode[1], not_14_out, not_15_out, opcode[4], opcode[5], not_16_out);
  and and_5 (jal, opcode[0], opcode[1], opcode[2], opcode[3], not_17_out, opcode[5], opcode[6]);
  and and_6 (brchEn, opcode[0], opcode[1], not_18_out, not_19_out, not_20_out, opcode[5], opcode[6]);
  and and_7 (lui, opcode[0], opcode[1], opcode[2], not_21_out, opcode[4], opcode[5], not_22_out);
  and and_8 (sys, opcode[0], opcode[1], not_23_out, not_24_out, opcode[4], opcode[5], opcode[6]);
  and and_9 (fence, opcode[0], opcode[1], opcode[2], opcode[3], not_25_out, not_26_out, not_27_out);
  and and_10 (jalr, opcode[0], opcode[1], opcode[2], not_28_out, not_29_out, opcode[5], opcode[6]);
  and and_11 (auipc, opcode[0], opcode[1], opcode[2], not_30_out, opcode[4], not_31_out, not_32_out);
  and and_12 (and_12_out, f3[1], not_33_out);
  not not_33 (not_33_out, f3[2]);
  not not_34 (not_34_out, f3[1]);
  and and_13 (and_13_out, f3[0], not_34_out, f3[2]);
  Multiplexer #(.width(3)) multiplexer_1 (.in0(3'b001), .in1(3'b010), .out(multiplexer_1_out), .sel(d_we));
  Multiplexer #(.width(3)) multiplexer_2 (.in0(3'b001), .in1(3'b011), .out(multiplexer_2_out), .sel(brchEn));
  Multiplexer #(.width(3)) multiplexer_3 (.in0(3'b001), .in1(3'b100), .out(multiplexer_3_out), .sel(or_1_out));
  or or_1 (or_1_out, lui, auipc);
  Multiplexer #(.width(3)) multiplexer_4 (.in0(3'b001), .in1(3'b101), .out(multiplexer_4_out), .sel(jal));
  or or_2 (or_2_out, f7[5], and_12_out);
  or or_3 (or_3_out, and_12_out, and_14_out);
  and and_14 (and_14_out, f7[5], and_13_out);
  or or_4 (or_4_out, jalr, jal);
  assign insType = multiplexer_1_out | multiplexer_2_out | multiplexer_3_out | multiplexer_4_out;  // OR_Gate or_5, 3 bits wide
  and and_15 (and_15_out, or_2_out, op);
  and and_16 (and_16_out, or_3_out, opi);
  Multiplexer #(.width(2)) multiplexer_5 (.in0(2'b00), .in1(2'b01), .out(multiplexer_5_out), .sel(d_rd));
  Multiplexer #(.width(2)) multiplexer_6 (.in0(2'b00), .in1(2'b10), .out(multiplexer_6_out), .sel(lui));
  Multiplexer #(.width(2)) multiplexer_7 (.in0(2'b00), .in1(2'b11), .out(multiplexer_7_out), .sel(or_4_out));
  not not_35 (not_35_out, f3[2]);
  not not_36 (not_36_out, f3[1]);
  and and_17 (and_17_out, not_35_out, not_36_out, not_37_out);
  not not_37 (not_37_out, f3[0]);
  not not_38 (not_38_out, f3[1]);
  and and_18 (and_18_out, f3[2], not_38_out, f3[0]);
  or or_6 (out_21, brchEn, and_15_out, and_16_out);
  assign selInRd = multiplexer_5_out | multiplexer_6_out | multiplexer_7_out;  // OR_Gate or_7, 2 bits wide
  or or_8 (or_8_out, and_17_out, and_18_out);
  and and_19 (and_19_out, and_18_out, opi);
  or or_9 (or_9_out, and_19_out, op);
  or or_10 (pcSrc, jal, jalr);
  or or_11 (or_11_out, sys, d_we, brchEn, fence);
  not not_39 (wEn, or_11_out);
  or or_12 (selS1Alu, jal, auipc);
  or or_13 (or_13_out, brchEn, op, fence);
  not not_40 (selS2Alu, or_13_out);
  and and_20 (altAlu, f7[5], or_8_out, or_9_out);
  Multiplexer #(.width(3)) multiplexer_8 (.in0(3'b000), .in1(f3), .out(opAlu), .sel(or_14_out));
  or or_14 (or_14_out, opi, brchEn, op);

  assign enPc = 1'b1;
  assign i_rd = 1'b1;

  // Other names for the same wires on the sheet: brch = brchEn; load = d_rd; store = d_we
endmodule

module signExtender (
  input  [31:0] din,
  input  [1:0] adr2,
  input  [2:0] exType,
  output [31:0] dout
);

  wire [7:0] multiplexer_1_out;
  wire [15:0] multiplexer_2_out;
  wire [31:0] bit_extender_1_out, bit_extender_2_out;

  Multiplexer #(.select(2), .width(8)) multiplexer_1 (
    .in0(din[7:0]), .in1(din[15:8]), .in2(din[23:16]), .in3(din[31:24]), .out(multiplexer_1_out), .sel(adr2));
  Multiplexer #(.width(16)) multiplexer_2 (.in0(din[15:0]), .in1(din[31:16]), .out(multiplexer_2_out), .sel(adr2[1]));
  assign bit_extender_1_out = {{24{multiplexer_1_out[7]}}, multiplexer_1_out};  // Bit_Extender bit_extender_1
  assign bit_extender_2_out = {{16{multiplexer_2_out[15]}}, multiplexer_2_out};  // Bit_Extender bit_extender_2
  Multiplexer #(.select(3), .width(32)) multiplexer_3 (
    .in0(bit_extender_1_out), .in1(bit_extender_2_out), .in2(din), .in3(din),
    .in4({{24{1'b0}}, multiplexer_1_out}), .in5({{16{1'b0}}, multiplexer_2_out}), .in6(din), .in7(din),
    .out(dout), .sel(exType));
endmodule
